# Fritzing sketch sketch (saved by Fritzing 0.7.12b)
breadboards: 1

parts:
  Pi1 = Adafruit Pi Cobbler
  VCC1 = 4 x AAA Battery Mount
  10k_R = LSM303 Breakout Board - Tilt-Compensated Compass
  US5881LUA_-_Hall_effect_sensor = mystery part, 3 pins [chip_label=US5881 spacing=300mil]
  R1_-_10K1 = 10k Ω Resistor [package=THT]

nets:
  N1: Pi1.5V0, VCC1.+, 10k_R.VCC, US5881LUA_-_Hall_effect_sensor.pin1, R1_-_10K1.Pin_1
  N2: Pi1.SDA0, 10k_R.SDA_M
  N3: Pi1.SCL0, 10k_R.SCL_M
  GND: Pi1.GND, VCC1.-, 10k_R.GND, US5881LUA_-_Hall_effect_sensor.pin2
  N4: Pi1.CE1, US5881LUA_-_Hall_effect_sensor.pin3, R1_-_10K1.Pin_0

custom parts:
  Adafruit Pi Cobbler: Adafruit Pi Cobbler GPIO Breakout for Raspberry Pi
